# Fritzing sketch RFID-RC522 (saved by Fritzing 0.9.5d)
breadboards: 1

parts:
  LED1 = LED - 5mm [color="Green (570nm)" package="5 mm [THT]"]
  LED2 = LED - 5mm [color="Red (633nm)" package="5 mm [THT]"]
  J1 = Piezo Speaker
  Bauteil1 = Arduino Uno (Rev3)
  Bauteil2 = RFID-RC522-v2
  R4 = Resistor [tolerance=±5% resistance=220 package=THT]
  R5 = Resistor [tolerance=±5% resistance=220 package=THT]

nets:
  N1: LED1.cathode, R5.Pin_1
  N2: LED1.anode, Bauteil1.D6_PWM
  N3: LED2.cathode, R4.Pin_1
  N4: LED2.anode, Bauteil1.D7
  GND: J1.pin1, Bauteil1.GND, Bauteil2.GND, R4.Pin_0, R5.Pin_0
  N5: J1.pin2, Bauteil1.D5_PWM
  N6: Bauteil1.D9_PWM, Bauteil2.RST
  N7: Bauteil1.D10_PWM/SS, Bauteil2.SDA
  N8: Bauteil1.D11_PWM/MOSI, Bauteil2.MOSI
  N9: Bauteil1.D12/MISO, Bauteil2.MISO
  N10: Bauteil1.D13/SCK, Bauteil2.SCK
  N11: Bauteil1.3V3, Bauteil2.3_3V

custom parts:
  RFID-RC522-v2: A simple China made RFID-RC522 Reader; do check the pin labels, as this is a MFRC522 based clone.
